# Fritzing sketch Anlage2 (saved by Fritzing 0.9.3b)

parts:
  Part3 = RFID-RC522-v2
  Bauteil2 = Arduino Yun
  U16 = mystery part, 2 pins [chip_label=M4]
  U17 = mystery part, 2 pins [chip_label=M3]
  U18 = mystery part, 2 pins [chip_label=M2]
  U19 = mystery part, 2 pins [chip_label=M1]
  U20 = mystery part, 3 pins [chip_label=A3]  # not connected
  U21 = mystery part, 3 pins [chip_label=A2]  # not connected
  U22 = mystery part, 3 pins [chip_label=A1]
  U23 = mystery part, 3 pins [chip_label=A0]
  U24 = mystery part, 3 pins [chip_label="IR Right"]
  U25 = mystery part, 3 pins [chip_label="IR Left"]
  U26 = mystery part, 2 pins [chip_label=M4]
  U27 = mystery part, 2 pins [chip_label=M3]
  U28 = mystery part, 2 pins [chip_label=M2]
  U29 = mystery part, 2 pins [chip_label=M1]
  Part4 = RFID-RC522-v2
  U30 = mystery part, 8 pins [chip_label="Wagen Signal Oben"]
  U31 = mystery part, 8 pins [chip_label="Wagen Signal Unten"]
  U35 = mystery part, 5 pins [chip_label="RFIDl Unten"]
  U34 = mystery part, 5 pins [chip_label="RFIDl Oben"]
  U32 = mystery part, 5 pins [chip_label="RFIDl Unten"]
  U33 = mystery part, 5 pins [chip_label="RFIDl Oben"]
  U36 = mystery part, 5 pins [chip_label="Motor Oben"]
  U37 = mystery part, 5 pins [chip_label="Motor Unten"]
  U38 = mystery part, 8 pins [chip_label="Wagen Signal Oben"]
  U39 = mystery part, 8 pins [chip_label="Wagen Signal Unten"]
  U40 = mystery part, 5 pins [chip_label="Motor Unten"]
  U41 = mystery part, 5 pins [chip_label="Motor Oben"]
  U42 = mystery part, 2 pins [chip_label=9V]
  U43 = mystery part, 2 pins [chip_label=9V]

nets:
  N1: Part3.SDA, U39.pin8
  N2: Part3.SCK, U39.pin7
  N3: Part3.MOSI, U39.pin6
  N4: Part3.MISO, U39.pin5
  N5: Part3.IRQ, U39.pin4
  N6: Part3.GND, U39.pin3
  N7: Part3.RST, U39.pin2
  N8: Part3.3_3V, U39.pin1
  N9: Bauteil2.ICSP_MISO, U32.pin3
  N10: Bauteil2.ICSP_SCK, U32.pin1
  N11: Bauteil2.ICSP_MOSI, U32.pin2
  N12: Bauteil2.GND, U32.pin4
  N13: Bauteil2.D9_PWM, U31.pin7
  N14: Bauteil2.D10_PWM/SS, U31.pin1
  N15: Bauteil2.D5_PWM, U33.pin2
  N16: Bauteil2.D6_PWM, U33.pin1
  N17: Bauteil2.3V3, U33.pin3
  N18: U16.pin1, U41.pin4
  N19: U16.pin2, U40.pin3
  N20: U17.pin1, U41.pin3
  N21: U17.pin2, U40.pin4
  N22: U18.pin1, U41.pin2
  N23: U18.pin2, U40.pin2
  N24: U19.pin1, U41.pin1
  N25: U19.pin2, U40.pin1
  N26: U22.pin1, U30.pin3
  N27: U22.pin2, U30.pin1
  N28: U22.pin3, U30.pin2
  N29: U23.pin1, U30.pin6
  N30: U23.pin2, U30.pin4
  N31: U23.pin3, U30.pin5
  N32: U24.pin1, U38.pin6
  N33: U24.pin2, U38.pin5
  N34: U24.pin3, U38.pin4
  N35: U25.pin1, U38.pin3
  N36: U25.pin2, U38.pin2
  N37: U25.pin3, U38.pin1
  N38: U26.pin1, U37.pin2
  N39: U26.pin2, U36.pin2
  N40: U27.pin1, U37.pin3
  N41: U27.pin2, U36.pin3
  N42: U28.pin1, U37.pin4
  N43: U28.pin2, U36.pin4
  N44: U29.pin1, U37.pin5
  N45: U29.pin2, U36.pin5
  N46: Part4.SDA, U34.pin1
  N47: Part4.SCK, U35.pin1
  N48: Part4.MOSI, U35.pin2
  N49: Part4.MISO, U35.pin3
  N50: Part4.IRQ, U35.pin4
  N51: Part4.RST, U34.pin2
  N52: Part4.3_3V, U34.pin3
  N53: U42.pin1, U43.pin2
  N54: U42.pin2, U43.pin1

custom parts:
  RFID-RC522-v2: A simple China made RFID-RC522 Reader; do check the pin labels, as this is a MFRC522 based clone.
