# Fritzing sketch RFID-Double (saved by Fritzing 0.9.2b)
breadboards: 1

parts:
  Part4 = RFID-RC522-v2
  Part5 = RFID-RC522-v2
  Bauteil2 = Arduino Yun

nets:
  N1: Part4.SDA, Bauteil2.D10_PWM/SS
  N2: Part4.SCK, Part5.SCK, Bauteil2.ICSP_SCK
  N3: Part4.MOSI, Part5.MOSI, Bauteil2.ICSP_MOSI
  N4: Part4.MISO, Part5.MISO, Bauteil2.ICSP_MISO
  GND: Part4.GND, Part5.GND, Bauteil2.GND
  N5: Part4.RST, Bauteil2.D9_PWM
  N6: Part4.3_3V, Part5.3_3V, Bauteil2.3V3
  N7: Part5.SDA, Bauteil2.D5_PWM
  N8: Part5.RST, Bauteil2.D4

custom parts:
  RFID-RC522-v2: A simple China made RFID-RC522 Reader; do check the pin labels, as this is a MFRC522 based clone.
