# Fritzing sketch RFID-Single (saved by Fritzing 0.9.2b)

parts:
  Bauteil1 = Arduino Yun
  Part3 = RFID-RC522-v2

nets:
  N1: Bauteil1.ICSP_MISO, Part3.MISO
  N2: Bauteil1.ICSP_SCK, Part3.SCK
  N3: Bauteil1.ICSP_MOSI, Part3.MOSI
  GND: Bauteil1.GND, Part3.GND
  N4: Bauteil1.D9_PWM, Part3.RST
  N5: Bauteil1.D10_PWM/SS, Part3.SDA
  N6: Bauteil1.3V3, Part3.3_3V

custom parts:
  RFID-RC522-v2: A simple China made RFID-RC522 Reader; do check the pin labels, as this is a MFRC522 based clone.
